// Digital circuit MEF01.dig as structural Verilog
module MEF01 (
  input  clk,
  output Q_2,
  output Q_1,
  output Q_0
);

  wire and_1_out, and_2_out, and_3_out, and_4_out, FF_0_nq, FF_2_nq, not_1_out, or_1_out, or_2_out, xor_1_out;

  D_FF FF_2 (.D(or_2_out), .C(clk), .Q(Q_2), .nQ(FF_2_nq));
  not not_1 (not_1_out, xor_1_out);
  xor xor_1 (xor_1_out, Q_2, Q_1);
  D_FF FF_1 (.D(or_1_out), .C(clk), .Q(Q_1));  // open: nQ
  or or_1 (or_1_out, and_2_out, and_1_out);
  or or_2 (or_2_out, and_4_out, and_3_out);
  and and_1 (and_1_out, FF_2_nq, Q_0);
  and and_2 (and_2_out, FF_0_nq, Q_1);
  and and_3 (and_3_out, Q_2, Q_0);
  and and_4 (and_4_out, FF_0_nq, Q_1);
  D_FF FF_0 (.D(not_1_out), .C(clk), .Q(Q_0), .nQ(FF_0_nq));

  // Notes on the sheet:
  //   Q_0^*
  //   Q_1^*
  //   Q_2^*
endmodule
