// Digital circuit aula12.dig as structural Verilog
module aula12 (
  input  R_nW,
  input  SEL_0,
  input  D_IN,
  input  SEL_1
);

  wire driverinvsel_1_out, driverinvsel_2_out, driverinvsel_3_out, driverinvsel_4_out, driverinvsel_5_out,
       nand_1_out, nand_2_out, nand_3_out, nand_4_out, not_1_out, not_2_out, not_3_out, not_4_out,
       rs_ff_as_1_q, rs_ff_as_2_q;

  not not_1 (not_1_out, R_nW);
  not not_2 (not_2_out, R_nW);
  nand nand_1 (nand_1_out, not_1_out, SEL_0);
  nand nand_2 (nand_2_out, SEL_0, R_nW);
  not not_3 (not_3_out, D_IN);
  nand nand_3 (nand_3_out, not_2_out, SEL_1);
  nand nand_4 (nand_4_out, SEL_1, R_nW);
  not not_4 (not_4_out, D_IN);
  assign driverinvsel_1_out = ~nand_1_out ? not_3_out : 1'bz;  // DriverInvSel driverinvsel_1
  assign driverinvsel_2_out = ~nand_1_out ? D_IN : 1'bz;  // DriverInvSel driverinvsel_2
  assign driverinvsel_3_out = ~nand_3_out ? not_4_out : 1'bz;  // DriverInvSel driverinvsel_3
  assign driverinvsel_4_out = ~nand_3_out ? D_IN : 1'bz;  // DriverInvSel driverinvsel_4
  RS_FF_AS rs_ff_as_1 (.S(driverinvsel_2_out), .R(driverinvsel_1_out), .Q(rs_ff_as_1_q));  // open: nQ
  RS_FF_AS rs_ff_as_2 (.S(driverinvsel_4_out), .R(driverinvsel_3_out), .Q(rs_ff_as_2_q));  // open: nQ
  LED D_0 (.in(rs_ff_as_1_q));
  LED D_1 (.in(rs_ff_as_2_q));
  assign driverinvsel_5_out = ~nand_2_out ? rs_ff_as_1_q : 1'bz;  // DriverInvSel driverinvsel_5
  assign driverinvsel_5_out = ~nand_4_out ? rs_ff_as_2_q : 1'bz;  // DriverInvSel driverinvsel_6
  LED D_OUT (.in(driverinvsel_5_out));
endmodule
