// Digital circuit contador4bit.dig as structural Verilog
module contador4bit (
  input  R_0,
  input  R_1,
  input  clk
);

  wire nand_1_out, s_0, s_1, s_2, s_3;

  nand nand_1 (nand_1_out, R_0, R_1);
  _74112 _74112_1 (
    .pin1(clk), .pin2(1'b1), .pin3(1'b1), .pin4(1'b1), .pin5(s_0), .pin8(1'b0), .pin9(s_1), .pin10(1'b1),
    .pin11(1'b1), .pin12(1'b1), .pin13(s_0), .pin14(nand_1_out), .pin15(nand_1_out), .pin16(1'b1));  // open: pin6, pin7
  LED out_3 (.in(s_3));
  LED out_1 (.in(s_1));
  LED out_2 (.in(s_2));
  LED out_0 (.in(s_0));
  _74112 _74112_2 (
    .pin1(s_1), .pin2(1'b1), .pin3(1'b1), .pin4(1'b1), .pin5(s_2), .pin8(1'b0), .pin9(s_3), .pin10(1'b1),
    .pin11(1'b1), .pin12(1'b1), .pin13(s_2), .pin14(nand_1_out), .pin15(nand_1_out), .pin16(1'b1));  // open: pin6, pin7
endmodule
