// Digital circuit NAND.dig as structural Verilog
module NAND (
  input  A,
  input  B,
  input  C
);

  wire nand_1_out, nand_2_out, nand_3_out, nand_4_out, nand_5_out, nand_6_out, nand_7_out, nand_8_out,
       nand_9_out, nand_10_out, nand_11_out, nand_12_out, nand_13_out;

  nand nand_1 (nand_1_out, A, B);
  nand nand_2 (nand_2_out, A, C);
  nand nand_3 (nand_3_out, B, C);
  nand nand_4 (nand_4_out, nand_1_out, nand_1_out);
  nand nand_5 (nand_5_out, nand_2_out, nand_2_out);
  nand nand_6 (nand_6_out, nand_3_out, nand_3_out);
  nand nand_7 (nand_7_out, nand_4_out, nand_4_out);
  nand nand_8 (nand_8_out, nand_5_out, nand_5_out);
  nand nand_9 (nand_9_out, nand_6_out, nand_6_out);
  nand nand_10 (nand_10_out, nand_8_out, nand_9_out);
  nand nand_11 (nand_11_out, nand_7_out, nand_7_out);
  nand nand_12 (nand_12_out, nand_10_out, nand_10_out);
  nand nand_13 (nand_13_out, nand_11_out, nand_12_out);
  LED S (.in(nand_13_out));
endmodule
