// Digital circuit TrabalhoSimpleCurcuit.dig as structural Verilog
module TrabalhoSimpleCurcuit (
  input  A,
  input  B,
  input  C
);

  wire and_1_out, and_2_out, and_3_out, not_1_out, or_1_out, or_2_out;

  and and_1 (and_1_out, A, B);
  and and_2 (and_2_out, A, C);
  and and_3 (and_3_out, B, C);
  not not_1 (not_1_out, and_1_out);
  or or_1 (or_1_out, and_2_out, and_3_out);
  or or_2 (or_2_out, not_1_out, or_1_out);
  LED S (.in(or_2_out));
endmodule
