// Digital circuit pr03_prob1-1.dig as structural Verilog
module pr03_prob1_1 (
  input  A,
  input  B,
  input  C,
  input  D
);

  wire and_1_out, and_2_out, and_3_out, or_1_out;

  and and_1 (and_1_out, A, B);
  and and_2 (and_2_out, D, B);
  and and_3 (and_3_out, and_2_out, C);
  or or_1 (or_1_out, and_1_out, and_3_out);
  LED led_1 (.in(or_1_out));
endmodule
