// Digital circuit pr03_prob1-2.dig as structural Verilog
module pr03_prob1_2 (
  input  A,
  input  B,
  input  C,
  input  D
);

  wire AND_pin3, AND_pin6, AND_pin8, OR_pin3;

  _7408 AND (
    .pin1(A), .pin2(B), .pin3(AND_pin3), .pin4(D), .pin5(B), .pin6(AND_pin6), .pin7(1'b0), .pin8(AND_pin8),
    .pin9(AND_pin6), .pin10(C), .pin12(1'b0), .pin13(1'b0), .pin14(1'b1));  // open: pin11
  _7432 OR (
    .pin1(AND_pin3), .pin2(AND_pin8), .pin3(OR_pin3), .pin4(1'b0), .pin5(1'b0), .pin7(1'b0), .pin9(1'b0),
    .pin10(1'b0), .pin12(1'b0), .pin13(1'b0), .pin14(1'b1));  // open: pin6, pin8, pin11
  LED S (.in(OR_pin3));
endmodule
