// Digital circuit pr3_prob2-1.dig as structural Verilog
module pr3_prob2_1 (
  input  X_1,
  input  X_2,
  input  X_3,
  input  X_1_2,
  input  X_2_2,
  input  X_3_2,
  input  X_1_3,
  input  X_3_3
);

  wire and_1_out, and_2_out, and_3_out, and_4_out, and_5_out, and_6_out, and_7_out, and_8_out, and_9_out,
       not_1_out, not_2_out, not_3_out, not_4_out, not_5_out, not_6_out, not_7_out, not_8_out, or_1_out,
       or_2_out, or_3_out;

  not not_1 (not_1_out, X_1);
  not not_2 (not_2_out, X_1_2);
  not not_3 (not_3_out, X_1_3);
  not not_4 (not_4_out, X_2);
  not not_5 (not_5_out, X_3);
  not not_6 (not_6_out, X_2_2);
  not not_7 (not_7_out, X_3_2);
  not not_8 (not_8_out, X_3_3);
  and and_1 (and_1_out, not_3_out, X_3_3);
  and and_2 (and_2_out, X_1_3, not_8_out);
  and and_3 (and_3_out, not_1_out, X_3);
  and and_4 (and_4_out, not_4_out, X_3);
  and and_5 (and_5_out, X_2, not_5_out);
  and and_6 (and_6_out, not_2_out, X_2_2, not_7_out);
  and and_7 (and_7_out, X_1_2, not_6_out);
  and and_8 (and_8_out, X_1_2, X_3_2);
  and and_9 (and_9_out, not_6_out, X_3_2);
  or or_1 (or_1_out, and_1_out, and_2_out);
  or or_2 (or_2_out, and_3_out, and_4_out, and_5_out);
  or or_3 (or_3_out, and_6_out, and_7_out, and_8_out, and_9_out);
  LED S (.in(or_2_out));
  LED S_2 (.in(or_1_out));
  LED S_3 (.in(or_3_out));

  // Notes on the sheet:
  //   E1
  //   E2
  //   E3
  //   Ayrton Sousa Marinho
  //   Daniel Brito
  //   Emanoel Bezerra
endmodule
