// Digital circuit pr3_prob2-2.dig as structural Verilog
module pr3_prob2_2 (
  input  X_1,
  input  X_2,
  input  X_3,
  input  X_1_2,
  input  X_2_2,
  input  X_3_2,
  input  X_1_3,
  input  X_3_3,
  input  X_1_4,
  input  X_2_3,
  input  X_3_4,
  input  X_1_5,
  input  X_2_4,
  input  X_3_5,
  input  X_1_6,
  input  X_3_6
);

  wire _7432_1_pin3, _7432_1_pin6, and_1_out, and_2_out, and_3_out, and_4_out, and_5_out, and_6_out,
       and_7_out, and_8_out, and_9_out, AND_10_pin3, AND_10_pin6, AND_11_pin3, AND_11_pin6, AND_11_pin11,
       AND_12_pin3, AND_12_pin6, AND_12_pin8, AND_12_pin11, AND_13_pin3, not_1_out, not_2_out, not_3_out,
       not_4_out, not_5_out, not_6_out, not_7_out, not_8_out, NOT_9_pin2, NOT_9_pin4, NOT_10_pin2,
       NOT_10_pin4, NOT_10_pin6, NOT_11_pin2, NOT_11_pin4, NOT_11_pin6, or_1_out, or_2_out, or_3_out,
       OR_4_pin3, OR_5_pin3, OR_5_pin6, OR_5_pin11;

  not not_1 (not_1_out, X_1_2);
  not not_2 (not_2_out, X_2_2);
  not not_3 (not_3_out, X_1_3);
  not not_4 (not_4_out, X_1);
  not not_5 (not_5_out, X_3_2);
  not not_6 (not_6_out, X_3_3);
  and and_1 (and_1_out, not_3_out, X_3_3);
  and and_2 (and_2_out, X_1_3, not_6_out);
  not not_7 (not_7_out, X_2);
  not not_8 (not_8_out, X_3);
  and and_3 (and_3_out, not_1_out, X_2_2, not_5_out);
  and and_4 (and_4_out, X_1_2, not_2_out);
  and and_5 (and_5_out, X_1_2, X_3_2);
  and and_6 (and_6_out, not_2_out, X_3_2);
  or or_1 (or_1_out, and_1_out, and_2_out);
  and and_7 (and_7_out, not_4_out, X_3);
  and and_8 (and_8_out, not_7_out, X_3);
  and and_9 (and_9_out, X_2, not_8_out);
  or or_2 (or_2_out, and_3_out, and_4_out, and_5_out, and_6_out);
  or or_3 (or_3_out, and_7_out, and_8_out, and_9_out);
  LED S (.in(or_2_out));
  LED S_2 (.in(or_1_out));
  LED S_3 (.in(or_3_out));
  _7404 NOT_9 (
    .pin1(X_1_6), .pin2(NOT_9_pin2), .pin3(X_3_6), .pin4(NOT_9_pin4), .pin5(1'b0), .pin7(1'b0), .pin9(1'b0),
    .pin11(1'b0), .pin13(1'b0), .pin14(1'b1));  // open: pin6, pin8, pin10, pin12
  _7408 AND_10 (
    .pin1(NOT_9_pin2), .pin2(X_3_6), .pin3(AND_10_pin3), .pin4(X_1_6), .pin5(NOT_9_pin4), .pin6(AND_10_pin6),
    .pin7(1'b0), .pin9(1'b0), .pin10(1'b0), .pin12(1'b0), .pin13(1'b0), .pin14(1'b1));  // open: pin8, pin11
  _7404 NOT_10 (
    .pin1(X_1_4), .pin2(NOT_10_pin2), .pin3(X_2_3), .pin4(NOT_10_pin4), .pin5(X_3_4), .pin6(NOT_10_pin6),
    .pin7(1'b0), .pin9(1'b0), .pin11(1'b0), .pin13(1'b0), .pin14(1'b1));  // open: pin8, pin10, pin12
  _7408 AND_11 (
    .pin1(NOT_10_pin2), .pin2(X_3_4), .pin3(AND_11_pin3), .pin4(NOT_10_pin4), .pin5(X_3_4),
    .pin6(AND_11_pin6), .pin7(1'b0), .pin9(1'b0), .pin10(1'b0), .pin11(AND_11_pin11), .pin12(NOT_10_pin6),
    .pin13(X_2_3), .pin14(1'b1));  // open: pin8
  _7404 NOT_11 (
    .pin1(X_1_5), .pin2(NOT_11_pin2), .pin3(X_2_4), .pin4(NOT_11_pin4), .pin5(X_3_5), .pin6(NOT_11_pin6),
    .pin7(1'b0), .pin9(1'b0), .pin11(1'b0), .pin13(1'b0), .pin14(1'b1));  // open: pin8, pin10, pin12
  _7408 AND_12 (
    .pin1(NOT_11_pin2), .pin2(X_2_4), .pin3(AND_12_pin3), .pin4(X_1_5), .pin5(NOT_11_pin4),
    .pin6(AND_12_pin6), .pin7(1'b0), .pin8(AND_12_pin8), .pin9(X_3_5), .pin10(X_1_5), .pin11(AND_12_pin11),
    .pin12(NOT_11_pin6), .pin13(AND_12_pin3), .pin14(1'b1));
  _7408 AND_13 (
    .pin1(NOT_11_pin4), .pin2(X_3_5), .pin3(AND_13_pin3), .pin4(1'b0), .pin5(1'b0), .pin7(1'b0), .pin9(1'b0),
    .pin10(1'b0), .pin12(1'b0), .pin13(1'b0), .pin14(1'b1));  // open: pin6, pin8, pin11
  LED E_1 (.in(_7432_1_pin6));
  _7432 _7432_1 (
    .pin1(AND_11_pin3), .pin2(AND_11_pin6), .pin3(_7432_1_pin3), .pin4(_7432_1_pin3), .pin5(AND_11_pin11),
    .pin6(_7432_1_pin6), .pin7(1'b0), .pin9(1'b0), .pin10(1'b0), .pin12(1'b0), .pin13(1'b0), .pin14(1'b1));  // open: pin8, pin11
  _7432 OR_4 (
    .pin1(AND_10_pin3), .pin2(AND_10_pin6), .pin3(OR_4_pin3), .pin4(1'b0), .pin5(1'b0), .pin7(1'b0),
    .pin9(1'b0), .pin10(1'b0), .pin12(1'b0), .pin13(1'b0), .pin14(1'b1));  // open: pin6, pin8, pin11
  _7432 OR_5 (
    .pin1(AND_12_pin11), .pin2(AND_12_pin6), .pin3(OR_5_pin3), .pin4(AND_13_pin3), .pin5(AND_12_pin8),
    .pin6(OR_5_pin6), .pin7(1'b0), .pin9(1'b0), .pin10(1'b0), .pin11(OR_5_pin11), .pin12(OR_5_pin6),
    .pin13(OR_5_pin3), .pin14(1'b1));  // open: pin8
  LED E_3 (.in(OR_4_pin3));
  LED E_2 (.in(OR_5_pin11));

  // Notes on the sheet:
  //   E2
  //   E3
  //   E1
  //   Ayrton Sousa Marinho
  //   Daniel Brito
  //   Emanoel Bezerra
  //   E_1
endmodule
