// Digital circuit pr06_p4.dig as structural Verilog
module pr06_p4 (
  input  clk
);

  wire and_1_out, jk_ff_as_1_nq, jk_ff_as_1_q, jk_ff_as_2_nq, jk_ff_as_2_q, jk_ff_as_3_nq, jk_ff_as_3_q,
       jk_ff_as_4_nq, not_1_out;

  LED q_3 (.in(jk_ff_as_4_nq));
  JK_FF_AS jk_ff_as_1 (
    .Set(and_1_out), .J(1'b1), .C(clk), .K(1'b1), .Clr(and_1_out), .Q(jk_ff_as_1_q), .nQ(jk_ff_as_1_nq));
  LED q_1 (.in(jk_ff_as_2_nq));
  LED q_2 (.in(jk_ff_as_3_nq));
  LED q_0 (.in(jk_ff_as_1_nq));
  and and_1 (and_1_out, jk_ff_as_4_nq, jk_ff_as_2_nq, not_1_out);
  JK_FF_AS jk_ff_as_2 (
    .Set(and_1_out), .J(1'b1), .C(jk_ff_as_1_q), .K(1'b1), .Clr(and_1_out), .Q(jk_ff_as_2_q),
    .nQ(jk_ff_as_2_nq));
  not not_1 (not_1_out, jk_ff_as_1_nq);
  JK_FF_AS jk_ff_as_3 (
    .Set(and_1_out), .J(1'b1), .C(jk_ff_as_2_q), .K(1'b1), .Clr(and_1_out), .Q(jk_ff_as_3_q),
    .nQ(jk_ff_as_3_nq));
  JK_FF_AS jk_ff_as_4 (
    .Set(and_1_out), .J(1'b1), .C(jk_ff_as_3_q), .K(1'b1), .Clr(and_1_out), .nQ(jk_ff_as_4_nq));  // open: Q
endmodule
