// Digital circuit CI_COUNTER.dig as structural Verilog
module CI_COUNTER (
  input  clk
);

  wire _7476_1_pin2, _7476_1_pin10, _7476_1_pin11, _7476_1_pin14, _7476_2_pin6, _7476_2_pin10, _7476_2_pin14,
       not_1_out, not_2_out;

  _7476 _7476_1 (
    .pin1(clk), .pin2(_7476_1_pin2), .pin3(_7476_1_pin2), .pin4(1'b1), .pin5(1'b1), .pin6(1'b1),
    .pin7(_7476_1_pin2), .pin8(_7476_1_pin2), .pin9(1'b1), .pin10(_7476_1_pin10), .pin11(_7476_1_pin11),
    .pin12(1'b1), .pin13(1'b0), .pin14(_7476_1_pin14), .pin15(1'b1), .pin16(1'b1));
  and and_1 (_7476_1_pin2, _7476_2_pin10, not_2_out, not_1_out, _7476_1_pin14);
  not not_1 (not_1_out, _7476_1_pin10);
  not not_2 (not_2_out, _7476_2_pin14);
  _7476 _7476_2 (
    .pin1(_7476_1_pin11), .pin2(_7476_1_pin2), .pin3(_7476_1_pin2), .pin4(1'b1), .pin5(1'b1),
    .pin6(_7476_2_pin6), .pin7(_7476_1_pin2), .pin8(_7476_1_pin2), .pin9(1'b1), .pin10(_7476_2_pin10),
    .pin11(1'b1), .pin12(1'b1), .pin13(1'b0), .pin14(_7476_2_pin14), .pin15(_7476_2_pin6), .pin16(1'b1));
  LED q1 (.in(_7476_1_pin14));
  LED q2 (.in(_7476_1_pin10));
  LED q3 (.in(_7476_2_pin14));
  LED q4 (.in(_7476_2_pin10));

  // Notes on the sheet:
  //   clk: Hz: 4
endmodule
